# Fritzing sketch schematic (saved by Fritzing 0.9.4)
breadboards: 1

parts:
  LED2 = RGB LED (com. cathode, rgb) [package="5 mm [THT]"]
  R2 = Resistor [tolerance=±5% resistance=220 package=THT]
  R3 = Resistor [tolerance=±5% resistance=220 package=THT]
  R4 = Resistor [tolerance=±5% resistance=220 package=THT]
  Raspberry_Pi_1 = Raspberry Pi 3 [part_number=RPI-3-V1.2]

nets:
  N1: LED2.red_anode, R2.Pin_0
  N2: LED2.green_anode, R3.Pin_0
  N3: LED2.blue_anode, R4.Pin_0
  N4: R2.Pin_1, Raspberry_Pi_1.GPIO17
  N5: R3.Pin_1, Raspberry_Pi_1.GPIO27
  N6: R4.Pin_1, Raspberry_Pi_1.GPIO22
