# Fritzing sketch schematic_combined (saved by Fritzing 0.9.4)
breadboards: 1

parts:
  LED2 = RGB LED (com. cathode, rgb) [package="5 mm [THT]"]
  R2 = Resistor [tolerance=±5% resistance=220 package=THT]
  R3 = Resistor [tolerance=±5% resistance=220 package=THT]
  Raspberry_Pi_1 = Raspberry Pi 3 [part_number=RPI-3-V1.2]
  RHT1 = Humidity and Temperature Sensor RHT03
  R5 = Resistor [tolerance=±5% resistance=10k package=THT]
  R4 = Resistor [tolerance=±5% resistance=220 package=THT]
  S1 = Momentary Switch [package=ksa_sealed_tac_switch]

nets:
  N1: LED2.red_anode, R2.Pin_0
  N2: LED2.green_anode, R3.Pin_0
  N3: LED2.blue_anode, R4.Pin_0
  N4: R2.Pin_1, Raspberry_Pi_1.GPIO17
  N5: R3.Pin_1, Raspberry_Pi_1.GPIO27
  3V3: Raspberry_Pi_1.3v3, RHT1.Vcc, R5.Pin_1
  N6: Raspberry_Pi_1.GPIO4, RHT1.Data-signal, R5.Pin_0
  N7: Raspberry_Pi_1.GPIO22, R4.Pin_1
  N8: Raspberry_Pi_1.GPIO10, S1.4
  N9: Raspberry_Pi_1.GND, RHT1.GND_2, S1.2
